// Digital circuit cpu.dig as structural Verilog
module cpu (
  input  clk
);

  wire add_2_c_o, AddrSelect, and_1_out, AssertA, AssertAlu, AssertB, AssertMemory, AssertTemp, Carry, CfSHL,
       CfSHR, comparator_1_eq, driver_1_out, FlagsEnable, JumpEnable, LoadA, LoadB, LoadIR, LoadMAR,
       LoadMemory, LoadPC, LoadTemp, not_1_out, Zero;
  wire [1:0] comparator_2_eq, RightSelect, Sequencer_out, ShiftSelect;
  wire [2:0] BusAssert, CarrySelect, LogicSelect;
  wire [3:0] bitcount_1_out, Decode_d_2;
  wire [4:0] bitextender_1_out;
  wire [6:0] SHL_out;
  wire [6:4] Decode_d;
  wire [7:0] A_q, add_1_s, add_2_s, AddressBus, and_2_out, B_q, driver_2_out, IR_q, MAR_q, multiplexer_1_out,
       multiplexer_3_out, multiplexer_4_out, multiplexer_5_out, not_2_out, or_1_out, Output_Register_q, PC_q,
       rom_1_d, Temp_q, xor_1_out;
  wire [7:1] SHR_out;

  Comparator #(.Bits(8)) comparator_1 (.a({8{1'b1}}), .b(AddressBus), .eq(comparator_1_eq));  // open: gt, lt
  not not_1 (not_1_out, AddressBus[7]);
  assign driver_1_out = 1'b1 ? AddressBus[7] : 1'bz;  // Driver driver_1
  Register #(.Bits(8)) PC (.D(multiplexer_1_out), .C(clk), .en(LoadPC), .Q(PC_q));
  ROM #(.AddrBits(7), .isProgramMemory("true"), .Bits(8)) rom_1 (.A(AddressBus[6:0]), .sel(not_1_out), .D(rom_1_d));
  RAMSinglePortSel #(.AddrBits(8), .Bits(8)) ramsingleportsel_1 (
    .A(AddressBus), .CS(1'b1), .WE(LoadMemory), .OE(driver_1_out), .D(rom_1_d));
  and and_1 (and_1_out, comparator_1_eq, LoadMemory);
  Multiplexer #(.Bits(8)) multiplexer_1 (
    .sel(JumpEnable), .in_0(add_1_s), .in_1(driver_2_out), .out(multiplexer_1_out));
  // Probe on PC_q
  Multiplexer #(.Bits(8)) multiplexer_2 (.sel(AddrSelect), .in_0(PC_q), .in_1(MAR_q), .out(AddressBus));
  Register #(.Bits(8)) Output_Register (.D(rom_1_d), .C(clk), .en(and_1_out), .Q(Output_Register_q));
  Add #(.Bits(8)) add_1 (.a(PC_q), .b(8'h1), .c_i(1'b0), .s(add_1_s));  // open: c_o
  // Probe on Output_Register_q
  Register #(.Bits(8)) MAR (.D(driver_2_out), .C(clk), .en(LoadMAR), .Q(MAR_q));
  assign driver_2_out = LoadMemory ? rom_1_d : 8'bz;  // Driver driver_2
  Driver #(.Bits(8)) driver_3 (.in(driver_2_out), .en(AssertMemory));  // open: out
  Register #(.Bits(8)) IR (.D(driver_2_out), .C(clk), .en(LoadIR), .Q(IR_q));
  assign driver_2_out = AssertAlu ? add_2_s : 8'bz;  // Driver driver_4
  assign driver_2_out = AssertA ? A_q : 8'bz;  // Driver driver_5
  assign driver_2_out = AssertB ? B_q : 8'bz;  // Driver driver_6
  assign driver_2_out = AssertTemp ? Temp_q : 8'bz;  // Driver driver_7
  Counter #(.Bits(2)) Sequencer (.en(1'b1), .C(clk), .clr(1'b0), .out(Sequencer_out));  // open: ovf
  Register #(.Bits(8)) A (.D(driver_2_out), .C(clk), .en(LoadA), .Q(A_q));
  Register #(.Bits(8)) B (.D(driver_2_out), .C(clk), .en(LoadB), .Q(B_q));
  Register #(.Bits(8)) Temp (.D(driver_2_out), .C(clk), .en(LoadTemp), .Q(Temp_q));
  BitExtender #(.inputBits(1), .outputBits(5)) bitextender_1 (.in(IR_q[7]), .out(bitextender_1_out));
  // Probe on IR_q[4:0]
  // Probe on A_q
  Multiplexer #(.Selector_Bits(2), .Bits(8)) multiplexer_3 (
    .sel(RightSelect), .in_0(A_q), .in_1(B_q), .in_2(Temp_q), .in_3({bitextender_1_out, IR_q[7:5]}),
    .out(multiplexer_3_out));
  // Probe on {Zero, Carry, IR_q[4:0], Sequencer_out}
  BarrelShifter #(.Bits(8)) SHL (.in(A_q), .shift(4'b0001), .out({CfSHL, SHL_out}));
  BarrelShifter #(.Bits(8), .direction("right")) SHR (.in(A_q), .shift(4'b0001), .out({SHR_out, CfSHR}));
  assign and_2_out = A_q & multiplexer_3_out;  // And and_2, 8 bits wide
  assign or_1_out = A_q | multiplexer_3_out;  // Or or_1, 8 bits wide
  assign xor_1_out = A_q ^ multiplexer_3_out;  // XOr xor_1, 8 bits wide
  assign not_2_out = ~A_q;  // Not not_2, 8 bits wide
  ROM #(.AddrBits(9), .Bits(14)) Decode (
    .A({Zero, Carry, IR_q[4:0], Sequencer_out}), .sel(1'b1),
    .D({Decode_d_2, BusAssert, Decode_d, RightSelect, AddrSelect, LoadPC}));
  Multiplexer #(.Selector_Bits(2), .Bits(8)) multiplexer_4 (
    .sel(ShiftSelect), .in_0({CfSHL, SHL_out}), .in_1(A_q), .in_2({8{1'b0}}), .in_3({SHR_out, CfSHR}),
    .out(multiplexer_4_out));
  // Probe on {Decode_d_2, BusAssert, Decode_d, RightSelect, AddrSelect, LoadPC}
  Multiplexer #(.Selector_Bits(3), .Bits(8)) multiplexer_5 (
    .sel(LogicSelect), .in_0(and_2_out), .in_1(or_1_out), .in_2(xor_1_out), .in_3(not_2_out),
    .in_4(multiplexer_3_out), .in_5({8{1'b1}}), .in_6({8{1'b0}}), .in_7({8{1'b0}}), .out(multiplexer_5_out));
  Decoder #(.Selector_Bits(3)) decoder_1 (
    .sel(Decode_d), .out_0(LoadTemp), .out_1(LoadMAR), .out_2(LoadA), .out_3(LoadB), .out_4(LoadIR),
    .out_5(JumpEnable), .out_6(LoadMemory));  // open: out_7
  Add #(.Bits(8)) add_2 (.a(multiplexer_4_out), .b(multiplexer_5_out), .c_i(Carry), .s(add_2_s), .c_o(add_2_c_o));
  BitCount #(.Bits(8)) bitcount_1 (.in(add_2_s), .out(bitcount_1_out));
  Comparator #(.Bits(4)) comparator_2 (.a(4'b0000), .b(bitcount_1_out), .eq(comparator_2_eq[1]));  // open: gt, lt
  Multiplexer #(.Selector_Bits(3)) multiplexer_6 (
    .sel(CarrySelect), .in_0(add_2_c_o), .in_1(CfSHL), .in_2(CfSHR), .in_3(1'b0), .in_4(1'b1), .in_5(1'b1),
    .in_6(1'b1), .in_7(1'b1), .out(comparator_2_eq[0]));
  Decoder #(.Selector_Bits(3)) decoder_2 (
    .sel(BusAssert), .out_0(AssertAlu), .out_1(AssertA), .out_2(AssertB), .out_3(AssertMemory),
    .out_4(AssertTemp));  // open: out_5, out_6, out_7
  Register #(.Bits(2)) Flags (.D(comparator_2_eq), .C(clk), .en(FlagsEnable), .Q({Zero, Carry}));
  Multiplexer #(.Selector_Bits(4), .Bits(9)) multiplexer_7 (
    .sel(Decode_d_2), .in_0({9{1'b0}}), .in_1(9'h111), .in_2({9{1'b0}}), .in_3(9'h100), .in_4(9'h103),
    .in_5(9'h101), .in_6(9'h101), .in_7(9'h101), .in_8(9'h101), .in_9(9'h100), .in_10(9'h100),
    .in_11({9{1'b0}}), .in_12({9{1'b0}}), .in_13({9{1'b0}}), .in_14({9{1'b0}}), .in_15({9{1'b0}}),
    .out({FlagsEnable, CarrySelect, LogicSelect, ShiftSelect}));

  // Notes on the sheet:
  //   clk: Hz: 10
  //   rom_1 loads nops.bin
  //   Decode loads microcode.bin
endmodule
